// Logisim project CircuitProject.circ as structural Verilog: 1 circuit, main circuit main
module main (
  input  SW14,
  input  SW13,
  input  SW12,
  input  SW11,
  input  SW10,
  input  SW9,
  input  SW8,
  input  SW15,
  input  SW6,
  input  SW5,
  input  SW4,
  input  SW3,
  input  SW2,
  input  SW1,
  input  SW0,
  input  SW7
);

  wire or_1_out, or_2_out, or_3_out, or_4_out, or_5_out, or_6_out, or_7_out, or_8_out, or_9_out, or_10_out,
       register_1_q, undriven, xor_1_out;
  wire [6:0] multiplexer_1_out, multiplexer_2_out;
  wire [6:1] xor_2_out, xor_8_out;

  or or_1 (or_1_out, SW11, or_5_out);
  or or_2 (or_2_out, SW12, or_1_out);
  or or_3 (or_3_out, SW13, or_2_out);
  or or_4 (or_4_out, SW9, SW8);
  or or_5 (or_5_out, SW10, or_4_out);
  or or_6 (or_6_out, SW4, or_10_out);
  or or_7 (or_7_out, SW5, or_6_out);
  Register #(.width(1)) register_1 (.D(xor_1_out), .en(undriven), .Q(register_1_q));  // open: clk, clr
  xor xor_1 (xor_1_out, SW7, SW15);
  xor xor_2 (xor_2_out[1], SW8, SW9);
  xor xor_3 (xor_2_out[2], or_4_out, SW10);
  xor xor_4 (xor_2_out[3], or_5_out, SW11);
  xor xor_5 (xor_2_out[4], or_1_out, SW12);
  xor xor_6 (xor_2_out[5], or_2_out, SW13);
  xor xor_7 (xor_2_out[6], or_3_out, SW14);
  or or_8 (or_8_out, SW1, SW0);
  or or_9 (or_9_out, SW2, or_8_out);
  or or_10 (or_10_out, SW3, or_9_out);
  xor xor_8 (xor_8_out[1], SW0, SW1);
  xor xor_9 (xor_8_out[2], or_8_out, SW2);
  xor xor_10 (xor_8_out[3], or_9_out, SW3);
  xor xor_11 (xor_8_out[4], or_10_out, SW4);
  xor xor_12 (xor_8_out[5], or_6_out, SW5);
  xor xor_13 (xor_8_out[6], or_7_out, SW6);
  Multiplexer #(.width(7)) multiplexer_1 (
    .in0({SW14, SW13, SW12, SW11, SW10, SW9, SW8}), .in1({xor_2_out, SW8}), .out(multiplexer_1_out),
    .sel(SW15));
  Multiplexer #(.width(7)) multiplexer_2 (
    .in0({SW6, SW5, SW4, SW3, SW2, SW1, SW0}), .in1({xor_8_out, SW0}), .out(multiplexer_2_out), .sel(SW7));
endmodule
